// Logisim project GT-2200.circ as structural Verilog: 9 circuits, main circuit Datapath
module Datapath (
  input  CLK,
  input  [1:0] Func,
  input  LdA,
  input  LdPC,
  input  LdB,
  input  LdMAR,
  input  RegSelLo,
  input  DrPC,
  input  DrALU,
  input  WrREG,
  input  WrMEM,
  input  RegSelHi,
  input  LdIR,
  input  DrREG,
  input  DrMEM,
  input  DrOFF,
  input  LdCMP,
  output [3:0] IR_31_28,
  output CmpOut
);

  wire comparator_1_eq, comparator_1_gt, multiplexer_1_out, not_1_out;
  wire [3:0] IR_q, IR_q_3, Mode, Regno;
  wire [19:4] IR_q_2;
  wire [23:0] bit_extender_1_out;
  wire [31:0] A_q, ALU_output, B_q, bit_extender_2_out, controlled_buffer_1_out, MAR_q, PC_q, ram_1_data,
       Regfile_data_out;

  Register #(.width(32)) PC (.D(controlled_buffer_1_out), .en(LdPC), .Q(PC_q), .clk(CLK));  // open: clr
  assign controlled_buffer_1_out = DrPC ? PC_q : 32'bz;  // Controlled_Buffer controlled_buffer_1
  Comparator #(.width(32)) comparator_1 (
    .a(controlled_buffer_1_out), .b({32{1'b0}}), .gt(comparator_1_gt), .eq(comparator_1_eq));  // open: lt
  Register #(.width(32)) A (.D(controlled_buffer_1_out), .en(LdA), .Q(A_q), .clk(CLK));  // open: clr
  _32_Bit_ALU ALU (.a(A_q), .b(B_q), .operation(Func), .\output (ALU_output));
  assign controlled_buffer_1_out = DrALU ? ALU_output : 32'bz;  // Controlled_Buffer controlled_buffer_2
  Register #(.width(32)) B (.D(controlled_buffer_1_out), .en(LdB), .Q(B_q), .clk(CLK));  // open: clr
  Multiplexer #(.disabled(0), .enable("false")) multiplexer_1 (
    .in0(comparator_1_eq), .in1(comparator_1_gt), .out(multiplexer_1_out), .sel(Mode[0]));
  RegFile Regfile (
    .Data_In(controlled_buffer_1_out), .WrREG(WrREG), .CLK(CLK), .Regno(Regno), .Data_Out(Regfile_data_out));
  assign controlled_buffer_1_out = DrREG ? Regfile_data_out : 32'bz;  // Controlled_Buffer controlled_buffer_3
  Register #(.width(1)) CmpREG (.D(multiplexer_1_out), .en(LdCMP), .Q(CmpOut), .clk(CLK));  // open: clr
  Register #(.width(32)) MAR (.D(controlled_buffer_1_out), .en(LdMAR), .Q(MAR_q), .clk(CLK));  // open: clr
  Bit_Extender #(.in_width(32), .out_width(24)) bit_extender_1 (.in(MAR_q), .out(bit_extender_1_out));
  RAM #(.addrWidth(24), .dataWidth(32), .bus("separate")) ram_1 (
    .addr(bit_extender_1_out), .din(controlled_buffer_1_out), .data(ram_1_data), .str(WrMEM), .clk(CLK),
    .ld(not_1_out));  // open: sel, clr
  not not_1 (not_1_out, WrMEM);
  assign controlled_buffer_1_out = DrMEM ? ram_1_data : 32'bz;  // Controlled_Buffer controlled_buffer_4
  Register #(.width(32)) IR (
    .D(controlled_buffer_1_out), .en(LdIR), .Q({IR_31_28, Mode, IR_q_3, IR_q_2, IR_q}), .clk(CLK));  // open: clr
  Multiplexer #(.select(2), .width(4), .disabled(0), .enable("false")) multiplexer_2 (
    .in0(Mode), .in1(IR_q_3), .in2(IR_q), .out(Regno), .sel({RegSelHi, RegSelLo}));  // open: in3
  assign bit_extender_2_out = {{12{IR_q_2[19]}}, {IR_q_2, IR_q}};  // Bit_Extender bit_extender_2
  assign controlled_buffer_1_out = DrOFF ? bit_extender_2_out : 32'bz;  // Controlled_Buffer controlled_buffer_5
endmodule

module _1_Bit_Adder (
  input  a,
  input  b,
  input  carry_in,
  output sum,
  output carry_out
);

  wire and_1_out, and_2_out, xor_1_out;

  xor xor_1 (xor_1_out, a, b);
  and and_1 (and_1_out, b, a);
  xor xor_2 (sum, xor_1_out, carry_in);
  and and_2 (and_2_out, xor_1_out, carry_in);
  or or_1 (carry_out, and_1_out, and_2_out);
endmodule

module _4_Bit_Adder (
  input  [3:0] a,
  input  [3:0] b,
  input  carry_in,
  output [3:0] sum,
  output carry_out
);

  wire n1_bit_adder_1_carry_out, n1_bit_adder_2_carry_out, n1_bit_adder_3_carry_out;

  _1_Bit_Adder u_1_bit_adder_1 (
    .a(a[0]), .b(b[0]), .carry_in(carry_in), .sum(sum[0]), .carry_out(n1_bit_adder_1_carry_out));
  _1_Bit_Adder u_1_bit_adder_2 (
    .a(a[1]), .b(b[1]), .carry_in(n1_bit_adder_1_carry_out), .sum(sum[1]),
    .carry_out(n1_bit_adder_2_carry_out));
  _1_Bit_Adder u_1_bit_adder_3 (
    .a(a[2]), .b(b[2]), .carry_in(n1_bit_adder_2_carry_out), .sum(sum[2]),
    .carry_out(n1_bit_adder_3_carry_out));
  _1_Bit_Adder u_1_bit_adder_4 (
    .a(a[3]), .b(b[3]), .carry_in(n1_bit_adder_3_carry_out), .sum(sum[3]), .carry_out(carry_out));
endmodule

module _16_Bit_Adder (
  input  [15:0] a,
  input  [15:0] b,
  input  carry_in,
  output [15:0] sum,
  output carry_out
);

  wire n4_bit_adder_1_carry_out, n4_bit_adder_2_carry_out, n4_bit_adder_3_carry_out;

  _4_Bit_Adder u_4_bit_adder_1 (
    .a(a[3:0]), .b(b[3:0]), .carry_in(carry_in), .sum(sum[3:0]), .carry_out(n4_bit_adder_1_carry_out));
  _4_Bit_Adder u_4_bit_adder_2 (
    .a(a[7:4]), .b(b[7:4]), .carry_in(n4_bit_adder_1_carry_out), .sum(sum[7:4]),
    .carry_out(n4_bit_adder_2_carry_out));
  _4_Bit_Adder u_4_bit_adder_3 (
    .a(a[11:8]), .b(b[11:8]), .carry_in(n4_bit_adder_2_carry_out), .sum(sum[11:8]),
    .carry_out(n4_bit_adder_3_carry_out));
  _4_Bit_Adder u_4_bit_adder_4 (
    .a(a[15:12]), .b(b[15:12]), .carry_in(n4_bit_adder_3_carry_out), .sum(sum[15:12]), .carry_out(carry_out));
endmodule

module _32_Bit_Adder (
  input  [31:0] a,
  input  [31:0] b,
  input  carry_in,
  output [31:0] sum,
  output carry_out
);

  wire n16_bit_adder_1_carry_out;

  _16_Bit_Adder u_16_bit_adder_1 (
    .a(a[15:0]), .b(b[15:0]), .carry_in(carry_in), .sum(sum[15:0]), .carry_out(n16_bit_adder_1_carry_out));
  _16_Bit_Adder u_16_bit_adder_2 (
    .a(a[31:16]), .b(b[31:16]), .carry_in(n16_bit_adder_1_carry_out), .sum(sum[31:16]), .carry_out(carry_out));
endmodule

module _32_Bit_ALU (
  input  [31:0] a,
  input  [31:0] b,
  input  [1:0] operation,
  output [31:0] \output 
);

  wire adder_1_cout, adder_2_cout, subtractor_1_bout;
  wire [31:0] adder_1_out, adder_2_out, nand_1_out, subtractor_1_out;

  Adder #(.width(32)) adder_1 (.a(a), .b(b), .out(adder_1_out), .cin(1'b0), .cout(adder_1_cout));
  Subtractor #(.width(32)) subtractor_1 (.a(a), .b(b), .out(subtractor_1_out), .bin(1'b0), .bout(subtractor_1_bout));
  assign nand_1_out = ~(a & b);  // NAND_Gate nand_1, 32 bits wide
  Adder #(.width(32)) adder_2 (.a(a), .b(32'h1), .out(adder_2_out), .cin(1'b0), .cout(adder_2_cout));
  Multiplexer #(.select(2), .width(32), .disabled(0), .enable("false")) multiplexer_1 (
    .in0(adder_1_out), .in1(subtractor_1_out), .in2(nand_1_out), .in3(adder_2_out), .out(\output ),
    .sel(operation));
  // also tied to GND on the sheet: {subtractor_1_bout, adder_2_cout, adder_1_cout}
endmodule

module RegFile (
  input  [31:0] Data_In,
  input  WrREG,
  input  [3:0] Regno,
  input  CLK,
  output [31:0] Data_Out
);

  wire and_1_out, and_2_out, and_3_out, and_4_out, and_5_out, and_6_out, and_7_out, and_8_out, and_9_out,
       and_10_out, and_11_out, and_12_out, and_13_out, and_14_out, and_15_out, and_16_out, decoder_1_out0,
       decoder_1_out1, decoder_1_out2, decoder_1_out3, decoder_1_out4, decoder_1_out5, decoder_1_out6,
       decoder_1_out7, fp, k0, ra, s0, s1, s2, sp, t2;
  wire [31:0] a0, a1, a2, at, fp_q, k0_q, ra_q, s0_q, s1_q, s2_q, sp_q, t0, t1, t2_q, v0, zero;

  Decoder #(.select(4), .enable("false")) decoder_1 (
    .out0(decoder_1_out0), .out1(decoder_1_out1), .out2(decoder_1_out2), .out3(decoder_1_out3),
    .out4(decoder_1_out4), .out5(decoder_1_out5), .out6(decoder_1_out6), .out7(decoder_1_out7), .out8(t2),
    .out9(s0), .out10(s1), .out11(s2), .out12(k0), .out13(sp), .out14(fp), .out15(ra), .sel(Regno));
  and and_1 (and_1_out, 1'b0, decoder_1_out0);
  and and_2 (and_2_out, WrREG, decoder_1_out1);
  and and_3 (and_3_out, WrREG, decoder_1_out2);
  and and_4 (and_4_out, WrREG, decoder_1_out3);
  and and_5 (and_5_out, WrREG, decoder_1_out4);
  and and_6 (and_6_out, WrREG, decoder_1_out5);
  and and_7 (and_7_out, WrREG, decoder_1_out6);
  and and_8 (and_8_out, WrREG, decoder_1_out7);
  Register #(.width(32)) u_zero (.D(Data_In), .en(and_1_out), .Q(zero), .clk(CLK));  // open: clr
  Register #(.width(32)) u_at (.D(Data_In), .en(and_2_out), .Q(at), .clk(CLK));  // open: clr
  Register #(.width(32)) u_v0 (.D(Data_In), .en(and_3_out), .Q(v0), .clk(CLK));  // open: clr
  Register #(.width(32)) u_a0 (.D(Data_In), .en(and_4_out), .Q(a0), .clk(CLK));  // open: clr
  Register #(.width(32)) u_a1 (.D(Data_In), .en(and_5_out), .Q(a1), .clk(CLK));  // open: clr
  Register #(.width(32)) u_a2 (.D(Data_In), .en(and_6_out), .Q(a2), .clk(CLK));  // open: clr
  Register #(.width(32)) u_t0 (.D(Data_In), .en(and_7_out), .Q(t0), .clk(CLK));  // open: clr
  Register #(.width(32)) u_t1 (.D(Data_In), .en(and_8_out), .Q(t1), .clk(CLK));  // open: clr
  and and_9 (and_9_out, WrREG, t2);
  and and_10 (and_10_out, WrREG, s0);
  and and_11 (and_11_out, WrREG, s1);
  and and_12 (and_12_out, WrREG, s2);
  and and_13 (and_13_out, WrREG, k0);
  and and_14 (and_14_out, WrREG, sp);
  and and_15 (and_15_out, WrREG, fp);
  and and_16 (and_16_out, WrREG, ra);
  Register #(.width(32)) u_t2 (.D(Data_In), .en(and_9_out), .Q(t2_q), .clk(CLK));  // open: clr
  Register #(.width(32)) u_s0 (.D(Data_In), .en(and_10_out), .Q(s0_q), .clk(CLK));  // open: clr
  Register #(.width(32)) u_s1 (.D(Data_In), .en(and_11_out), .Q(s1_q), .clk(CLK));  // open: clr
  Register #(.width(32)) u_s2 (.D(Data_In), .en(and_12_out), .Q(s2_q), .clk(CLK));  // open: clr
  Register #(.width(32)) u_k0 (.D(Data_In), .en(and_13_out), .Q(k0_q), .clk(CLK));  // open: clr
  Register #(.width(32)) u_sp (.D(Data_In), .en(and_14_out), .Q(sp_q), .clk(CLK));  // open: clr
  Register #(.width(32)) u_fp (.D(Data_In), .en(and_15_out), .Q(fp_q), .clk(CLK));  // open: clr
  Register #(.width(32)) u_ra (.D(Data_In), .en(and_16_out), .Q(ra_q), .clk(CLK));  // open: clr
  Multiplexer #(.select(4), .width(32), .disabled(0), .enable("false")) multiplexer_1 (
    .in0(zero), .in1(at), .in2(v0), .in3(a0), .in4(a1), .in5(a2), .in6(t0), .in7(t1), .in8(t2_q), .in9(s0_q),
    .in10(s1_q), .in11(s2_q), .in12(k0_q), .in13(sp_q), .in14(fp_q), .in15(ra_q), .out(Data_Out), .sel(Regno));
endmodule

module Microcontroller (
  input  CLK,
  input  [3:0] IR_31_28,
  input  CmpOut,
  output DrREG,
  output DrMEM,
  output DrALU,
  output DrPC,
  output DrOFF,
  output LdPC,
  output LdIR,
  output LdMAR,
  output LdA,
  output LdB,
  output LdCmp,
  output WrReg,
  output WrMEM,
  output RegSelLo,
  output RegSelHi,
  output ALULo,
  output ALUHi
);

  wire ChkCmp, NS0, NS1, NS2, NS3, NS4, NS5, OPTest;
  wire [5:0] multiplexer_1_out, rom_2_data, rom_3_data, State_Register_q;

  Register #(.width(6)) State_Register (
    .D(multiplexer_1_out), .en(1'b1), .Q(State_Register_q), .clk(CLK));  // open: clr
  Multiplexer #(.select(2), .width(6), .disabled(0), .enable("false")) multiplexer_1 (
    .in0({NS5, NS4, NS3, NS2, NS1, NS0}), .in1(rom_2_data), .in2(rom_3_data), .out(multiplexer_1_out),
    .sel({ChkCmp, OPTest}));  // open: in3
  ROM #(.addrWidth(6), .dataWidth(25)) rom_1 (
    .addr(State_Register_q),
    .data({ChkCmp, OPTest, ALUHi, ALULo, RegSelHi, RegSelLo, WrMEM, WrReg, LdCmp, LdB, LdA, LdMAR, LdIR, LdPC, DrOFF, DrPC, DrALU, DrMEM, DrREG, NS5, NS4, NS3, NS2, NS1, NS0}));  // open: sel
  ROM #(.addrWidth(4), .dataWidth(6)) rom_2 (.addr(IR_31_28), .data(rom_2_data));  // open: sel
  ROM #(.addrWidth(2), .dataWidth(6)) rom_3 (.addr({1'b0, CmpOut}), .data(rom_3_data));  // open: sel

  // Notes on the sheet:
  //   Main ROM
  //   Sequencer ROM
  //   Condition ROM
  //   contents of rom_1 (hex, n*v repeats v):
  //   6201 1082 600903 800000 84045 108046 20100 84048 8409 20100 8404b 10804c 420100 8404e 10804f 210110
  //   1000011 4212 600900 4214 8415 900 4217 8418 20100 8405a 841b 211c 20080 8405e 841f 2120 40040 a0222
  //   840 23
  //   contents of rom_2 (hex, n*v repeats v):
  //   4 7 a d 13 16 0 0 19 1d 0 0 21 0 0 23
  //   contents of rom_3 (hex, n*v repeats v):
  //   0 11
endmodule

module Processor (
);

  wire ALUHi, ALULo, clock_1_out, datapath_1_cmpout, DrALU, DrMEM, DrOFF, DrPC, DrREG, LdA, LdB, LdCMP, LdIR,
       LdMAR, LdPC, RegSelHi, RegSelLo, WrMEM, WrREG;
  wire [3:0] datapath_1_ir_31_28;

  Microcontroller Microcontroller (
    .IR_31_28(datapath_1_ir_31_28), .CmpOut(datapath_1_cmpout), .DrREG(DrREG), .DrMEM(DrMEM), .DrALU(DrALU),
    .DrPC(DrPC), .DrOFF(DrOFF), .LdPC(LdPC), .LdIR(LdIR), .LdMAR(LdMAR), .CLK(clock_1_out), .LdA(LdA),
    .LdB(LdB), .LdCmp(LdCMP), .WrReg(WrREG), .WrMEM(WrMEM), .RegSelLo(RegSelLo), .RegSelHi(RegSelHi),
    .ALULo(ALULo), .ALUHi(ALUHi));
  Clock clock_1 (.out(clock_1_out));
  Datapath datapath_1 (
    .CLK(clock_1_out), .Func({ALUHi, ALULo}), .LdA(LdA), .LdPC(LdPC), .LdB(LdB), .LdMAR(LdMAR),
    .RegSelLo(RegSelLo), .DrPC(DrPC), .DrALU(DrALU), .WrREG(WrREG), .WrMEM(WrMEM), .RegSelHi(RegSelHi),
    .LdIR(LdIR), .DrREG(DrREG), .DrMEM(DrMEM), .DrOFF(DrOFF), .LdCMP(LdCMP), .IR_31_28(datapath_1_ir_31_28),
    .CmpOut(datapath_1_cmpout));
endmodule
